# Fritzing sketch devre_cizimi (saved by Fritzing 0.9.3b)

parts:
  Parça1 = Arduino Uno (Rev3) - ICSP
  LED2 = LEDs [package=led10mm]
  LED3 = LEDs [package=led10mm]
  J1 = Piezo Speaker
  BAT1 = BC9VPC [package=bc9vpc]  # not connected
  S1 = KY-026

nets:
  N1: Parça1.A0, S1.pin1
  N2: Parça1.D11_PWM/MOSI, LED2.A
  N3: Parça1.D12/MISO, LED3.A
  N4: Parça1.D13/SCK, J1.pin2
  N5: Parça1.GND, LED2.C, LED3.C, J1.pin1, S1.pin2
  N6: Parça1.5V, S1.pin3

notes:
  Yeşil LED
  Kırmızı LED
  Arduino için pil
  BUZZER
  UV Alev Sensörü

custom parts:
  KY-026: ky-026 flame sensor module
